// Logisim project lr4.circ as structural Verilog: 3 circuits, main circuit main
module main (
  input  A,
  input  B,
  input  C,
  output Transfer,
  output Sum
);

  wire not_1_out, not_2_out, not_3_out, or_1_out, or_2_out, or_3_out, or_4_out, or_5_out, or_6_out, or_7_out;

  and and_1 (Transfer, or_1_out, or_2_out, or_3_out);
  or or_1 (or_1_out, A, B);
  or or_2 (or_2_out, A, C);
  or or_3 (or_3_out, B, C);
  not not_1 (not_1_out, B);
  not not_2 (not_2_out, A);
  not not_3 (not_3_out, C);
  or or_4 (or_4_out, not_2_out, C, not_1_out);
  or or_5 (or_5_out, not_2_out, not_3_out, B);
  or or_6 (or_6_out, A, not_3_out, not_1_out);
  or or_7 (or_7_out, C, B, A);
  and and_2 (Sum, or_4_out, or_5_out, or_6_out, or_7_out);
endmodule

module EightBitSum (
  input  [7:0] in_1,
  input  [7:0] in_2,
  output [7:0] out_3
);

  wire main_1_transfer, main_2_transfer, main_3_transfer, main_4_transfer, main_5_transfer, main_6_transfer,
       main_7_transfer, main_8_transfer;

  main main_1 (.A(in_1[7]), .B(in_2[7]), .C(main_2_transfer), .Transfer(main_1_transfer), .Sum(out_3[7]));
  main main_2 (.A(in_1[6]), .B(in_2[6]), .C(main_3_transfer), .Transfer(main_2_transfer), .Sum(out_3[6]));
  main main_3 (.A(in_1[5]), .B(in_2[5]), .C(main_4_transfer), .Transfer(main_3_transfer), .Sum(out_3[5]));
  main main_4 (.A(in_1[4]), .B(in_2[4]), .C(main_5_transfer), .Transfer(main_4_transfer), .Sum(out_3[4]));
  main main_5 (.A(in_1[3]), .B(in_2[3]), .C(main_6_transfer), .Transfer(main_5_transfer), .Sum(out_3[3]));
  main main_6 (.A(in_1[2]), .B(in_2[2]), .C(main_7_transfer), .Transfer(main_6_transfer), .Sum(out_3[2]));
  main main_7 (.A(in_1[1]), .B(in_2[1]), .C(main_8_transfer), .Transfer(main_7_transfer), .Sum(out_3[1]));
  main main_8 (.A(in_1[0]), .B(in_2[0]), .C(main_1_transfer), .Transfer(main_8_transfer), .Sum(out_3[0]));
endmodule

module Step (
  input  A,
  input  B,
  input  C,
  input  D,
  input  [3:0] in_5,
  output [3:0] out_6
);

  wire and_1_out, and_2_out, and_3_out, and_4_out, and_5_out, and_6_out, and_7_out, not_1_out, not_2_out,
       not_3_out, or_3_out;

  and and_1 (and_1_out, in_5[3], in_5[1]);
  not not_1 (not_1_out, in_5[3]);
  not not_2 (not_2_out, in_5[2]);
  not not_3 (not_3_out, in_5[1]);
  and and_2 (and_2_out, in_5[2], not_3_out);
  or or_1 (out_6[3], and_1_out, and_2_out);
  and and_3 (and_3_out, in_5[3], in_5[2]);
  or or_2 (out_6[2], and_3_out, and_4_out);
  and and_4 (and_4_out, not_1_out, not_2_out);
  and and_5 (and_5_out, in_5[3], not_2_out);
  and and_6 (and_6_out, in_5[3], in_5[1]);
  or or_3 (or_3_out, and_5_out, and_6_out);
  or or_4 (out_6[1], or_3_out, and_7_out);
  and and_7 (and_7_out, not_2_out, in_5[1]);

  assign out_6[0] = in_5[0];

  // Notes on the sheet:
  //   out_6: pull=up
endmodule
