// Logisim project lr5.circ as structural Verilog: 1 circuit, main circuit main
module main (
  input  F,
  output [3:0] out_2
);

  wire and_1_out, and_2_out, and_3_out, clock_1_out, t_ff_1_qn, t_ff_2_qn, t_ff_3_qn;

  Clock clock_1 (.out(clock_1_out));
  T_Flip_Flop t_ff_1 (.T(F), .clk(clock_1_out), .Q(out_2[0]), .Qn(t_ff_1_qn));  // open: reset, preset
  and and_1 (and_1_out, F, t_ff_1_qn);
  T_Flip_Flop t_ff_2 (.T(and_1_out), .clk(clock_1_out), .Q(out_2[1]), .Qn(t_ff_2_qn));  // open: reset, preset
  T_Flip_Flop t_ff_3 (.T(and_2_out), .clk(clock_1_out), .Q(out_2[2]), .Qn(t_ff_3_qn));  // open: reset, preset
  T_Flip_Flop t_ff_4 (.T(and_3_out), .clk(clock_1_out), .Q(out_2[3]));  // open: Qn, reset, preset
  and and_2 (and_2_out, t_ff_2_qn, t_ff_1_qn, F);
  and and_3 (and_3_out, t_ff_3_qn, t_ff_2_qn, t_ff_1_qn, F);
endmodule
